# Fritzing sketch model_1 (saved by Fritzing 1.0.4)

parts:
  Part2 = KY-037 High Sensitivity Sound Detection Module [package="Breakout board"]
  Part3 = Arduino Uno (Rev3) - ICSP
  LED1 = LED - 5mm [color="Green (555nm)" current=0.030A package="5 mm [THT]"]
  Part4 = Arduino Nano (Rev3.0)
  Part5 = KY-037 High Sensitivity Sound Detection Module [package="Breakout board"]
  R3 = Resistor [tolerance=±5% resistance=330 package="0603 [SMD]"]
  LED2 = LED - 5mm [color="Green (555nm)" current=0.030A package="5 mm [THT]"]
  R4 = Resistor [tolerance=±5% resistance=330 package="0603 [SMD]"]

nets:
  N1: Part2.A0, Part3.A0
  N2: Part2.G, Part3.GND, LED1.cathode
  N3: Part2.+, Part3.5V
  N4: Part3.D2, R4.Pin_1
  N5: Part4.GND, Part5.G, LED2.cathode
  N6: Part4.D2, R3.Pin_1
  N7: Part4.5V, Part5.+
  N8: Part4.A0, Part5.A0

custom parts:
  KY-037 High Sensitivity Sound Detection Module: KY-037 high sensitivity sound detection module is an analog/digital sensor that uses a condenser microphone to observe changes in environment noise.
